# Fritzing sketch HistoRdualESP32 (saved by Fritzing 0.9.3b)
stripboards: 1
perfboards: 1

parts:
  U1 = LuaNode32 / ESP32 [part_number=ESP32S-PIN30]
  U2 = LuaNode32 / ESP32 [part_number=ESP32S-PIN30]
  Součástka1 = MCU5102 I2S Stereo DAC  # not connected
  MCU5102_I2S_Stereo_DAC1_1 = MCU5102 I2S Stereo DAC  # not connected
  MCU5102_I2S_Stereo_DAC1_2 = MCU5102 I2S Stereo DAC  # not connected
  MCU5102_I2S_Stereo_DAC1_3 = MCU5102 I2S Stereo DAC  # not connected
  MCU5102_I2S_Stereo_DAC1_4 = MCU5102 I2S Stereo DAC  # not connected
  Součástka2 = LCD1602-I2C
  MCU5102_I2S_Stereo_DAC1 = MCU5102 I2S Stereo DAC
  Součástka6 = MCU5102 I2S Stereo DAC  # not connected
  MCU5102_I2S_Stereo_DAC1_1_2 = MCU5102 I2S Stereo DAC  # not connected
  MCU5102_I2S_Stereo_DAC1_2_2 = MCU5102 I2S Stereo DAC  # not connected
  MCU5102_I2S_Stereo_DAC1_3_2 = MCU5102 I2S Stereo DAC  # not connected
  MCU5102_I2S_Stereo_DAC1_4_2 = MCU5102 I2S Stereo DAC  # not connected
  XY-USB1 = XY-USB4
  microSD1 = MicroSD Card Module
  Součástka3 = Digital FM Radio Receiver
  Součástka4 = Si4713 Stereo FM Transmitter
  MCU5102_I2S_Stereo_DAC2 = MCU5102 I2S Stereo DAC
  Součástka7 = MCU5102 I2S Stereo DAC  # not connected
  MCU5102_I2S_Stereo_DAC2_1 = MCU5102 I2S Stereo DAC  # not connected
  MCU5102_I2S_Stereo_DAC2_2 = MCU5102 I2S Stereo DAC  # not connected
  MCU5102_I2S_Stereo_DAC2_3 = MCU5102 I2S Stereo DAC  # not connected
  MCU5102_I2S_Stereo_DAC2_4 = MCU5102 I2S Stereo DAC  # not connected
  5V = male pin header, 8 pins [form="♂ (male)"]
  3_3V_-_1 = male pin header, 8 pins [form="♂ (male)"]
  GND = male pin header, 10 pins [form="♂ (male)"]
  3_3V_-_2 = male pin header, 8 pins [form="♂ (male)"]
  SDA = male pin header, 3 pins [form="♂ (male)"]
  SCL = male pin header, 3 pins [form="♂ (male)"]
  Součástka5 = Adafruit Si5351A Clock Generator [part_number="Adafruit #2045"]
  KY-1 = Keyes Relay [package=THT]
  RelaySig = male pin header, 2 pins [form="♂ (male)"]
  5V_to_9V-12V_step-up = MT3608 Boost No usb
  5V_2 = male pin header, 5 pins [form="♂ (male)"]
  GND_2 = male pin header, 5 pins [form="♂ (male)"]
  Součástka8 = TRRS 3.5mm Jack Breakout
  SCL_2 = male pin header, 3 pins [form="♂ (male)"]
  SDA_2 = male pin header, 3 pins [form="♂ (male)"]
  SDA1 = male pin header, 3 pins [form="♂ (male)"]
  SCL1 = male pin header, 3 pins [form="♂ (male)"]
  SCL2 = male pin header, 3 pins [form="♂ (male)"]
  SDA2 = male pin header, 3 pins [form="♂ (male)"]
  RelaySig1 = male pin header, 2 pins [form="♂ (male)"]  # not connected
  GND1 = male pin header, 3 pins [form="♂ (male)"]
  5V1 = male pin header, 3 pins [form="♂ (male)"]
  MixerAudioIn = male pin header, 2 pins [form="♂ (male)"]
  MixerClkIn = male pin header, 2 pins [form="♂ (male)"]
  MixerRfOut = male pin header, 2 pins [form="♂ (male)"]
  AmplifierOut = male pin header, 2 pins [form="♂ (male)"]
  AmplifierIn = male pin header, 2 pins [form="♂ (male)"]
  Antena = male pin header, 1 pin [form="♂ (male)"]
  ANT1 = Antenna
  MixerPower = male pin header, 2 pins [form="♂ (male)"]
  AmplifierPower = male pin header, 2 pins [form="♂ (male)"]

nets:
  N1: U1.D25, MCU5102_I2S_Stereo_DAC1.connector8
  N2: U1.D26, MCU5102_I2S_Stereo_DAC1.connector6
  N3: U1.D27, MCU5102_I2S_Stereo_DAC1.connector7
  N4: U1.Vin, 5V.pin4
  N5: U1.3V3, 3_3V_-_1.pin8
  N6: U1.GND, GND.pin7
  N7: U1.D5, microSD1.CS
  N8: U1.D18, microSD1.SCK
  N9: U1.D19, microSD1.MOSI
  N10: U1.D21, SDA_2.pin2
  N11: U1.D22, SCL_2.pin2
  N12: U1.D23, microSD1.MISO
  N13: U2.D25, MCU5102_I2S_Stereo_DAC2.connector8
  N14: U2.D26, MCU5102_I2S_Stereo_DAC2.connector6
  N15: U2.D27, MCU5102_I2S_Stereo_DAC2.connector7
  N16: U2.GND, GND.pin6
  N17: U2.Vin, 5V.pin7
  N18: U2.3V3, 3_3V_-_2.pin1
  N19: U2.RX2, SDA_2.pin3
  N20: U2.TX2, SCL_2.pin3
  N21: U2.D5, Součástka4.CS
  N22: U2.D18, Součástka3.!RST
  N23: U2.D21, SDA1.pin1
  N24: U2.D22, SCL1.pin1
  N25: Součástka2.GND, GND_2.pin4
  N26: Součástka2.VCC, 5V_2.pin4
  N27: Součástka2.SDA, SDA.pin2
  N28: Součástka2.SCL, SCL.pin2
  N29: MCU5102_I2S_Stereo_DAC1.connector0, 3_3V_-_1.pin7
  N30: MCU5102_I2S_Stereo_DAC1.connector2, GND.pin5
  N31: XY-USB1.connector4, GND.pin10
  N32: XY-USB1.connector7, 5V.pin8
  N33: microSD1.GND, GND.pin4
  N34: microSD1.VCC, 5V.pin5
  N35: Součástka3.SCLK, SCL1.pin3
  N36: Součástka3.SDIO, SDA1.pin2
  N37: Součástka3.GND, GND.pin2
  N38: Součástka3.3.3V, 3_3V_-_2.pin2
  N39: Součástka4.VIN, 3_3V_-_2.pin3
  N40: Součástka4.GND, GND.pin1
  N41: Součástka4.SDA, SDA1.pin3
  N42: Součástka4.SCL, SCL1.pin2
  N43: MCU5102_I2S_Stereo_DAC2.connector0, 3_3V_-_2.pin4
  N44: MCU5102_I2S_Stereo_DAC2.connector2, GND.pin3
  N45: 5V.pin6, 5V1.pin3
  N46: GND.pin9, GND1.pin3
  N47: SDA.pin1, Součástka5.SDA
  N48: SCL.pin1, Součástka5.SCL
  N49: Součástka5.VIN, 5V_2.pin1
  N50: Součástka5.GND, GND_2.pin1, MixerClkIn.pin1
  N51: Součástka5.CLK0, MixerClkIn.pin2
  N52: KY-1.signal, RelaySig.pin1
  N53: KY-1.power, GND_2.pin2
  N54: KY-1.ground, 5V_2.pin2
  N55: KY-1.NC, AmplifierOut.pin2, Antena.pin1, ANT1.antenna_lead
  N56: KY-1.C, MixerRfOut.pin1
  N57: KY-1.NO, AmplifierIn.pin2
  N58: 5V_to_9V-12V_step-up.IN_(-), 5V_to_9V-12V_step-up.OUT_(-), GND_2.pin3, MixerPower.pin2, AmplifierPower.pin2
  N59: 5V_to_9V-12V_step-up.IN_(+), 5V_2.pin3
  N60: 5V_to_9V-12V_step-up.OUT_(+), MixerPower.pin1, AmplifierPower.pin1
  N61: Součástka8.SLEEVE, MixerAudioIn.pin2
  N62: Součástka8.RING1, Součástka8.TIP, MixerAudioIn.pin1
  N63: SCL_2.pin1, SCL2.pin3
  N64: SDA_2.pin1, SDA2.pin3
  N65: MixerRfOut.pin2, AmplifierIn.pin1

notes:
  AM transmitter
  AudioSwitcher - 3 in - 2 out
  HistoR dual ESP32
  HistoR Display

custom parts:
  LuaNode32 / ESP32: New Image for LuaNode32 DOIT ESP32 DEVKIT V1. Base parts from LuaNode32 / ESP32 ESP32 based LuaNode32 by G.Noorlander DOIT Esp32 DevKit v1 (30 pins long, 11 pins width) by Werner Rothschopf (modified by vanepp Dec 2018)
  LCD1602-I2C: A standard character display, usually with 2x16 characters. Comes in many colors with LCM1602 IIC attached.
  XY-USB4: USB adapter with power and data lines output pins. USB A, USB C, Micro USB.
  Si4713 Stereo FM Transmitter: Yaaar! Become your very own pirate radio station with this FM radio transmitter. This breakout board, based on the best-of-class Si4713, is an all-in-one stereo audio FM transmitter that can also transmit RDS/RBDS data!
  Adafruit Si5351A Clock Generator: Never hunt around for another crystal again, with the Si5351A clock generator breakout from Adafruit! This chip has a precision 25MHz crystal reference and internal PLL and dividers so it can generate just about any frequency, from <8KHz up to 150+ MHz. The Si5351A clock generator is an I2C controller clock generator. It uses the onboard precision clock to drive multiple PLL's and clock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
  Keyes Relay: The Keyes 5V relay module is suitable for SCM development, home appliance control. It uses a 5V~12V TIL control signal which can control DC / AC signal.
  MT3608 Boost No usb: Chip- MT3608 / B6289 DC to DC step up, power booster module. With adjustable output voltage. Current- 2A . || Input voltage- 2V-24V || Output voltage- 5V-28V Input interface- Inversed polarity- NO. || Led indicator- No.
